# Fritzing sketch Sketch (saved by Fritzing 0.9.2b)
breadboards: 2

parts:
  Pro_Micro1 = Pro Micro
  ENCODER1 = Rotary Encoder with Knob
  LCM1602_IIC1 = LCM1602 IIC [part_number="LCM1602 IIC" chip_label="LCM1602 IIC" package="DIP (Dual Inline) [THT]"]
  LCD1_20x5 = LCD screen
  R1 = Resistor [tolerance=±5% resistance=10k package=THT]
  R2 = Resistor [tolerance=±5% resistance=10k package=THT]
  R3 = Resistor [tolerance=±5% resistance=10k package=THT]
  U2 = 2.5mm Audio Jack [package=stereojack2.5mm_smd]  # not connected
  U1 = RELAY-2 [package=relay-g5v]  # not connected

nets:
  N1: Pro_Micro1.TX1, R3.Pin_0
  N2: Pro_Micro1.RX0, R2.Pin_0
  N3: Pro_Micro1.D2, LCM1602_IIC1.SDA
  N4: Pro_Micro1.D3, LCM1602_IIC1.SCL
  N5: Pro_Micro1.D4, ENCODER1.no_name_yet#4
  N6: ENCODER1.no_name_yet#2, ENCODER1.no_name_yet#5, LCM1602_IIC1.GND
  VSS: LCM1602_IIC1.VSS, LCD1_20x5.VSS
  VDD: LCM1602_IIC1.VDD, LCD1_20x5.VDD
  N7: LCM1602_IIC1.V0, LCD1_20x5.V0
  N8: LCM1602_IIC1.RS, LCD1_20x5.RS
  N9: LCM1602_IIC1.RW, LCD1_20x5.R/W
  N10: LCM1602_IIC1.E, LCD1_20x5.E
  N11: LCM1602_IIC1.D0, LCD1_20x5.DB0
  N12: LCM1602_IIC1.D1, LCD1_20x5.DB1
  N13: LCM1602_IIC1.D2, LCD1_20x5.DB2
  N14: LCM1602_IIC1.D3, LCD1_20x5.DB3
  N15: LCM1602_IIC1.D4, LCD1_20x5.DB4
  N16: LCM1602_IIC1.D5, LCD1_20x5.DB5
  N17: LCM1602_IIC1.D6, LCD1_20x5.DB6
  N18: LCM1602_IIC1.D7, LCD1_20x5.DB7
  N19: LCM1602_IIC1.A, LCD1_20x5.LED-
  N20: LCM1602_IIC1.K, LCD1_20x5.LED+
  N21: LCM1602_IIC1.VCC, R1.Pin_0
  N22: LCM1602_IIC1.LED_A, LCM1602_IIC1.LED_B

custom parts:
  Pro Micro: The SparkFun Pro Micro is a complete USB-based microcontoller development system, in a very small footprint, capable of implementing many types of projects. All programming can be done via the USB port.
  Rotary Encoder with Knob: Rotary Encoder with 1/4" Shaft and Knob
  LCM1602 IIC: I2C-Module to use a 1602 or 2004 LCD on with the wire.h libory Serial LCD Modul
  LCD screen: A standard character display, usually with 2x16 characters. Comes in many colors.
